# Fritzing sketch Ac and DC Components (saved by Fritzing 0.9.2b)

parts:
  ExpEYES_Hardware1 = ExpEYES , Pocket Science Lab
  C1 = Electrolytic Capacitor [capacitance=1µF package="100 mil [THT, electrolytic]"]
  R1 = Resistor [tolerance=±5% resistance=1k package="0805 [SMD]"]

nets:
  N1: ExpEYES_Hardware1.SQR1_8_6, ExpEYES_Hardware1.A1, C1.+
  N2: ExpEYES_Hardware1.GND, R1.Pin_1
  N3: ExpEYES_Hardware1.A2, C1.-, R1.Pin_0

custom parts:
  ExpEYES , Pocket Science Lab: ExpEYES - Experiments for Young Engineers and Scientists.
