# Fritzing sketch Cpacitance Measurement (saved by Fritzing 0.9.2b)

parts:
  ExpEYES_Hardware1 = ExpEYES , Pocket Science Lab
  Capacitor = Ceramic Capacitor [capacitance=1mF part_number="pF Range" package="0603 [SMD, multilayer]"]

nets:
  N1: ExpEYES_Hardware1.GND, Capacitor.1
  N2: ExpEYES_Hardware1.IN1_3, Capacitor.0

custom parts:
  ExpEYES , Pocket Science Lab: ExpEYES - Experiments for Young Engineers and Scientists.
