# Fritzing sketch DiodeIV (saved by Fritzing 0.9.2b)

parts:
  ExpEYES_Hardware1 = ExpEYES , Pocket Science Lab
  D1 = Diode [package=diode-1n4148]
  R1 = Resistor [tolerance=±5% resistance=1k package="0805 [SMD]"]

nets:
  N1: ExpEYES_Hardware1.IN1_3, D1.A, R1.Pin_0
  N2: ExpEYES_Hardware1.GND, D1.C
  N3: ExpEYES_Hardware1.PVS_12, R1.Pin_1

custom parts:
  ExpEYES , Pocket Science Lab: ExpEYES - Experiments for Young Engineers and Scientists.
