# Fritzing sketch Finding Resistance (saved by Fritzing 0.9.2b)

parts:
  ExpEYES_Hardware1 = ExpEYES , Pocket Science Lab
  Unknown_Resistor = Resistor [tolerance=±5% resistance=220 package="0805 [SMD]"]
  R1 = Resistor [tolerance=±5% resistance=1k package="0805 [SMD]"]

nets:
  N1: ExpEYES_Hardware1.IN1_3, Unknown_Resistor.Pin_0, R1.Pin_0
  N2: ExpEYES_Hardware1.GND, R1.Pin_1
  N3: ExpEYES_Hardware1.PVS_12, Unknown_Resistor.Pin_1

custom parts:
  ExpEYES , Pocket Science Lab: ExpEYES - Experiments for Young Engineers and Scientists.
