# Fritzing sketch Frequency of sound (saved by Fritzing 0.9.2b)

parts:
  ExpEYES_Hardware1 = ExpEYES , Pocket Science Lab
  Piezo = Piezo Speaker

nets:
  N1: ExpEYES_Hardware1.SQR1_8_6, Piezo.pin2
  N2: ExpEYES_Hardware1.GND, Piezo.pin1
  N3: ExpEYES_Hardware1.MIC, ExpEYES_Hardware1.A1

custom parts:
  ExpEYES , Pocket Science Lab: ExpEYES - Experiments for Young Engineers and Scientists.
