# Fritzing sketch Interference of Sound (saved by Fritzing 0.9.2b)

parts:
  ExpEYES_Hardware1 = ExpEYES , Pocket Science Lab
  Piezo_2 = Piezo Speaker
  Piezo_1 = Piezo Speaker  # not connected

nets:
  N1: ExpEYES_Hardware1.SQR2_9_7, Piezo_2.pin2
  N2: ExpEYES_Hardware1.GND#9, Piezo_2.pin1
  N3: ExpEYES_Hardware1.MIC, ExpEYES_Hardware1.A1

custom parts:
  ExpEYES , Pocket Science Lab: ExpEYES - Experiments for Young Engineers and Scientists.
  Piezo Speaker: Piezo
