# Fritzing sketch POV (saved by Fritzing 0.9.2b)

parts:
  ExpEYES_Hardware1 = ExpEYES , Pocket Science Lab
  LED = smd LED [color="Infrared (880nm)" package="0805 [SMD]"]

nets:
  N1: ExpEYES_Hardware1.GND, LED.cathode
  N2: ExpEYES_Hardware1.SQR1_8_6, LED.anode

custom parts:
  ExpEYES , Pocket Science Lab: ExpEYES - Experiments for Young Engineers and Scientists.
