# Fritzing sketch RC Differentiator (saved by Fritzing 0.9.2b)

parts:
  ExpEYES_Hardware1 = ExpEYES , Pocket Science Lab
  C2 = Electrolytic Capacitor [capacitance=1µF package="100 mil [THT, electrolytic]"]
  R1 = Resistor [tolerance=±5% resistance=220 package="0805 [SMD]"]

nets:
  N1: ExpEYES_Hardware1.A2, C2.+
  N2: ExpEYES_Hardware1.A1, C2.-, R1.Pin_1
  N3: ExpEYES_Hardware1.GND, R1.Pin_0

custom parts:
  ExpEYES , Pocket Science Lab: ExpEYES - Experiments for Young Engineers and Scientists.
