# Fritzing sketch Study of AC Circuits (saved by Fritzing 0.9.2b)

parts:
  ExpEYES_Hardware1 = ExpEYES , Pocket Science Lab
  R1 = Resistor [tolerance=±5% resistance=1k package="1206 [SMD]"]
  C1 = Electrolytic Capacitor [capacitance=1µF package="100 mil [THT, electrolytic]"]
  Coil_1 = Inductors [part_number="300mH , 5Ohms" package=npi75c]

nets:
  N1: ExpEYES_Hardware1.GND, R1.Pin_1
  N2: ExpEYES_Hardware1.SINE, ExpEYES_Hardware1.A1, Coil_1.2
  N3: ExpEYES_Hardware1.A2, R1.Pin_0, C1.-
  N4: C1.+, Coil_1.1

custom parts:
  ExpEYES , Pocket Science Lab: ExpEYES - Experiments for Young Engineers and Scientists.
