# Fritzing sketch Transient RC (saved by Fritzing 0.9.2b)

parts:
  ExpEYES_Hardware1 = ExpEYES , Pocket Science Lab
  R1 = Resistor [tolerance=±5% resistance=1k package="1206 [SMD]"]
  C1 = Electrolytic Capacitor [capacitance=1µF package="100 mil [THT, electrolytic]"]

nets:
  N1: ExpEYES_Hardware1.OD1_10, R1.Pin_1
  N2: ExpEYES_Hardware1.A1, R1.Pin_0, C1.+
  N3: ExpEYES_Hardware1.GND, C1.-

custom parts:
  ExpEYES , Pocket Science Lab: ExpEYES - Experiments for Young Engineers and Scientists.
