# Fritzing sketch Transient RL (saved by Fritzing 0.9.2b)

parts:
  ExpEYES_Hardware1 = ExpEYES , Pocket Science Lab
  R1 = Resistor [tolerance=±5% resistance=1k package="1206 [SMD]"]
  Coil_1 = Inductors [part_number="300mH 3000 turns" package=npi75c]

nets:
  N1: ExpEYES_Hardware1.OD1_10, R1.Pin_1
  N2: ExpEYES_Hardware1.A1, R1.Pin_0, Coil_1.1
  N3: ExpEYES_Hardware1.GND, Coil_1.2

custom parts:
  ExpEYES , Pocket Science Lab: ExpEYES - Experiments for Young Engineers and Scientists.
