# Fritzing sketch Transient RLC (saved by Fritzing 0.9.2b)

parts:
  ExpEYES_Hardware1 = ExpEYES , Pocket Science Lab
  Coil_1 = Inductors [part_number="130 mH , 600 Ohms" package=npi75c]
  C1 = Capacitor [part_number=0.1uF package=cap-pth-small2]

nets:
  N1: ExpEYES_Hardware1.OD1_10, Coil_1.1
  N2: ExpEYES_Hardware1.A1, Coil_1.2, C1.2
  N3: ExpEYES_Hardware1.GND, C1.1

custom parts:
  ExpEYES , Pocket Science Lab: ExpEYES - Experiments for Young Engineers and Scientists.
