# Fritzing sketch Transistor CE (saved by Fritzing 0.9.2b)
breadboards: 1

parts:
  ExpEYES_Hardware1 = ExpEYES , Pocket Science Lab
  Transistor = NPN-Transistor [package="TO92 [THT]"]
  R1 = Resistor [tolerance=±5% resistance=1k package="0805 [SMD]"]
  R2 = Resistor [tolerance=±5% resistance=220k part_number="200 k" package="0805 [SMD]"]
  C = Electrolytic Capacitor [capacitance=100µF package="200 mil [THT, electrolytic]"]

nets:
  N1: ExpEYES_Hardware1.IN1_3, Transistor.C, R1.Pin_0
  N2: ExpEYES_Hardware1.SQR1_8_6, R2.Pin_1
  N3: ExpEYES_Hardware1.GND, Transistor.E, C.-
  N4: ExpEYES_Hardware1.PVS_12, R1.Pin_1
  N5: Transistor.B, R2.Pin_0, C.+

custom parts:
  ExpEYES , Pocket Science Lab: ExpEYES - Experiments for Young Engineers and Scientists.
