# Fritzing sketch Water Resistance (saved by Fritzing 0.9.2b)

parts:
  ExpEYES_Hardware1 = ExpEYES , Pocket Science Lab
  R1 = Resistor [tolerance=±5% resistance=100k package="0402 [SMD]"]
  Water_Body = Resistor [tolerance=±5% resistance=150 package="0805 [SMD]"]

nets:
  N1: ExpEYES_Hardware1.SINE, ExpEYES_Hardware1.A2, Water_Body.Pin_1
  N2: ExpEYES_Hardware1.A1, R1.Pin_0, Water_Body.Pin_0
  N3: ExpEYES_Hardware1.GND, R1.Pin_1

custom parts:
  ExpEYES , Pocket Science Lab: ExpEYES - Experiments for Young Engineers and Scientists.
