# Fritzing sketch DiodeIV (saved by Fritzing 0.9.2b)
breadboards: 1

parts:
  IC1 = SEELablet
  Diode = Rectifier Diode [part_number=1N4001 package="300 mil [THT]"]
  R1 = Resistor [tolerance=±5% resistance=1k package="2512 [SMD]"]

nets:
  N1: IC1.CH3, Diode.anode, R1.Pin_0
  N2: IC1.PV1, R1.Pin_1
  N3: IC1.GND, Diode.cathode

custom parts:
  SEELablet: SEELablet provides an array of test equipment that includes an oscilloscope, waveform generators, frequency counters, Programmable voltage sources etc. along with a computer. The measurement/control functions are accessible from the Python programming language and GUI applications are also available for a variety of experiments. It also has essential applications like Web browser, Office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
